# Fritzing sketch LED_test (saved by Fritzing 0.9.3b)
breadboards: 1

parts:
  Raspberry_Pi_Zero1 = Raspberry Pi Zero
  R1 = Resistor [tolerance=±5% resistance=330 package=THT]
  LED1 = LED - 5mm [color="Red (633nm)" package="5 mm [THT]"]
  S1 = Pushbutton [package="[THT]"]
  R2 = Resistor [tolerance=±5% resistance=10k package=THT]

nets (from the breadboard view):
  3V3: Raspberry_Pi_Zero1.3v3, Raspberry_Pi_Zero1.3V3, S1.Pin_1, S1.Pin_2
  N1: Raspberry_Pi_Zero1.GPIO25, R1.Pin_0
  N2: Raspberry_Pi_Zero1.GPIO24, S1.Pin_3, S1.Pin_4, R2.Pin_1
  N3: Raspberry_Pi_Zero1.GND, LED1.cathode, R2.Pin_0
  N4: R1.Pin_1, LED1.anode

notes:
  Vf = 1.85V
  V = 3.3V
  Vf = 3.3 - 1.85 = 1.45V
  I = 1.45V / 220Ω = 6.6 mA
  10～20mAの電流が流れれば光る
